# Fritzing sketch picozoom (saved by Fritzing 0.9.10b)
circuit board: 11.2618cm x 10.7131cm

parts:
  Pico = Raspberry Pi Pico H
  Part1 = Adafruit TCA9548A
  OLED1 = 128x32 I2C Monochrome OLED Display
  OLED2 = 128x32 I2C Monochrome OLED Display
  OLED3 = 128x32 I2C Monochrome OLED Display
  OLED4 = 128x32 I2C Monochrome OLED Display
  OLED5 = 128x32 I2C Monochrome OLED Display
  S1 = Round Pushbutton
  X1 = USB Connectors [package=usb-a-s-silk-female]
  S2 = Round Pushbutton
  S3 = Round Pushbutton
  S4 = Round Pushbutton
  S5 = Round Pushbutton

nets:
  N1: Pico.VBUS, X1.VBUS
  VIN: Pico.VSYS, Part1.VCC, OLED1.VIN, OLED2.VIN, OLED3.VIN, OLED4.VIN, OLED5.VIN
  GND: Pico.GND, Part1.GND, OLED1.GND, OLED2.GND, OLED3.GND, OLED4.GND, OLED5.GND, S1.leg1, X1.GND, S2.leg1, S3.leg1, S4.leg1, S5.leg1
  N2: Pico.GP8, S5.leg0
  N3: Pico.GP7, S4.leg0
  N4: Pico.GP6, S3.leg0
  N5: Pico.GP5, S2.leg0
  N6: Pico.GP4, S1.leg0
  N7: Pico.GP3, X1.D-
  N8: Pico.GP2, X1.D+
  N9: Pico.GP1, Part1.INPUTSCL
  N10: Pico.GP0, Part1.INPUTSDA
  N11: Part1.3SDA, OLED5.SDA
  N12: Part1.3SCL, OLED5.SCL
  N13: Part1.4SDA, OLED2.SDA
  N14: Part1.4SCL, OLED2.SCL
  N15: Part1.5SDA, OLED4.SDA
  N16: Part1.5SCL, OLED4.SCL
  N17: Part1.6SDA, OLED3.SDA
  N18: Part1.6SCL, OLED3.SCL
  N19: Part1.7SDA, OLED1.SDA
  N20: Part1.7SCL, OLED1.SCL

notes:
  red VBUS
  black GND
  green D+
  white D-

custom parts:
  Raspberry Pi Pico H: Raspberry Pi Pico H. Based around the RP2040 microcontroller the Pico H is a low cost microcontroller device bringing Raspberry Pi quality, cost, and easy of use to the microcontroller space.
  Adafruit TCA9548A: You just found the perfect I2C sensor, and you want to wire up two or three or more of them to your Arduino when you realize "Uh oh, this chip has a fixed I2C address, and from what I know about I2C, you cannot have two devices with the same address on the same SDA/SCL pins!" Are you out of luck? You would be, if you didn't have this ultra-cool TCA9548A 1-to-8 I2C multiplexer! Finally, a way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
